// Logisim project regfile.circ as structural Verilog: 4 circuits, main circuit main
module main (
  input  [4:0] Read_Register_1,
  input  [4:0] Read_Register_2,
  input  [4:0] Write_Register,
  input  [31:0] Write_Data,
  input  Write_Enable,
  input  Clock,
  output [31:0] s0_Value,
  output [31:0] s1_Value,
  output [31:0] s2_Value,
  output [31:0] ra_Value,
  output [31:0] Read_Data_1,
  output [31:0] Read_Data_2
);

  wire [31:0] _0, _1, _2, _3, _4, _5, _6, _7, _8, _9, _10, _11, _12, _13, _14, _15, _19, _20, _21, _22, _23,
       _24, _25, _26, _27, _28, _29, _30;

  register_block register_block_1 (
    .Write_Data(Write_Data), .Clk(Clock), .Write_Enable(Write_Enable), .Write_Register(Write_Register),
    .out_5(_0), .out_6(_1), .out_7(_2), .out_8(_3), .out_9(_4), .out_10(_5), .out_11(_6), .out_12(_7),
    .out_13(_8), .out_14(_9), .out_15(_10), .out_16(_11), .out_17(_12), .out_18(_13), .out_19(_14),
    .out_20(_15), .out_21(s0_Value), .out_22(s1_Value), .out_23(s2_Value), .out_24(_19), .out_25(_20),
    .out_26(_21), .out_27(_22), .out_28(_23), .out_29(_24), .out_30(_25), .out_31(_26), .out_32(_27),
    .out_33(_28), .out_34(_29), .out_35(_30), .out_36(ra_Value));
  Register_Chooser register_chooser_1 (
    .reg_out(Read_Data_1), ._0(_0), .in_2(_1), .in_3(_2), .in_4(_3), .in_5(_4), .in_6(_5), .in_7(_6),
    .in_8(_7), .in_9(_8), .in_10(_9), .in_11(_10), .in_12(_11), .in_13(_12), .in_14(_13), .in_15(_14),
    ._15(_15), ._31(ra_Value), .in_19(_30), .in_20(_29), .in_21(_28), .in_22(_27), .in_23(_26), .in_24(_25),
    .in_25(_24), .in_26(_23), .in_27(_22), .in_28(_21), .in_29(_20), .in_30(_19), .in_31(s2_Value),
    .in_32(s1_Value), ._16(s0_Value), .reg_sel(Read_Register_1));
  Register_Chooser register_chooser_2 (
    .reg_out(Read_Data_2), ._0(_0), .in_2(_1), .in_3(_2), .in_4(_3), .in_5(_4), .in_6(_5), .in_7(_6),
    .in_8(_7), .in_9(_8), .in_10(_9), .in_11(_10), .in_12(_11), .in_13(_12), .in_14(_13), .in_15(_14),
    ._15(_15), ._31(ra_Value), .in_19(_30), .in_20(_29), .in_21(_28), .in_22(_27), .in_23(_26), .in_24(_25),
    .in_25(_24), .in_26(_23), .in_27(_22), .in_28(_21), .in_29(_20), .in_30(_19), .in_31(s2_Value),
    .in_32(s1_Value), ._16(s0_Value), .reg_sel(Read_Register_2));

  // Other names for the same wires on the sheet: _16[31:0] = s0_Value; _17[31:0] = s1_Value; _18[31:0] = s2_Value;
  //   _31[31:0] = ra_Value; clk = Clock; read_data1[31:0] = Read_Data_1; read_data2[31:0] = Read_Data_2;
  //   read_reg1[4:0] = Read_Register_1; read_reg2[4:0] = Read_Register_2; write_en = Write_Enable;
  //   write_reg[4:0] = Write_Register

  // Notes on the sheet:
  //   INPUTS to your circuit
  //   DON'T CHANGE THE LOCATIONS OF THE INPUTS AND OUTPUTS!
  //   These are DEBUG/TEST outputs from your circuit.
  //   OUTPUTS from your circuit
endmodule

module Register_Chooser (
  input  [31:0] _0,
  input  [31:0] in_2,
  input  [31:0] in_3,
  input  [31:0] in_4,
  input  [31:0] in_5,
  input  [31:0] in_6,
  input  [31:0] in_7,
  input  [31:0] in_8,
  input  [31:0] in_9,
  input  [31:0] in_10,
  input  [31:0] in_11,
  input  [31:0] in_12,
  input  [31:0] in_13,
  input  [31:0] in_14,
  input  [31:0] in_15,
  input  [31:0] _15,
  input  [4:0] reg_sel,
  input  [31:0] _31,
  input  [31:0] in_19,
  input  [31:0] in_20,
  input  [31:0] in_21,
  input  [31:0] in_22,
  input  [31:0] in_23,
  input  [31:0] in_24,
  input  [31:0] in_25,
  input  [31:0] in_26,
  input  [31:0] in_27,
  input  [31:0] in_28,
  input  [31:0] in_29,
  input  [31:0] in_30,
  input  [31:0] in_31,
  input  [31:0] in_32,
  input  [31:0] _16,
  output [31:0] reg_out
);

  Multiplexer #(.select(5), .width(32)) multiplexer_1 (
    .in0(_0), .in1(in_2), .in2(in_3), .in3(in_4), .in4(in_5), .in5(in_6), .in6(in_7), .in7(in_8), .in8(in_9),
    .in9(in_10), .in10(in_11), .in11(in_12), .in12(in_13), .in13(in_14), .in14(in_15), .in15(_15),
    .in16(_16), .in17(in_32), .in18(in_31), .in19(in_30), .in20(in_29), .in21(in_28), .in22(in_27),
    .in23(in_26), .in24(in_25), .in25(in_24), .in26(in_23), .in27(in_22), .in28(in_21), .in29(in_20),
    .in30(in_19), .in31(_31), .out(reg_out), .sel(reg_sel));  // open: en
endmodule

module register_block (
  input  [31:0] Write_Data,
  input  Clk,
  input  Write_Enable,
  input  [4:0] Write_Register,
  output [31:0] out_5,
  output [31:0] out_6,
  output [31:0] out_7,
  output [31:0] out_8,
  output [31:0] out_9,
  output [31:0] out_10,
  output [31:0] out_11,
  output [31:0] out_12,
  output [31:0] out_13,
  output [31:0] out_14,
  output [31:0] out_15,
  output [31:0] out_16,
  output [31:0] out_17,
  output [31:0] out_18,
  output [31:0] out_19,
  output [31:0] out_20,
  output [31:0] out_21,
  output [31:0] out_22,
  output [31:0] out_23,
  output [31:0] out_24,
  output [31:0] out_25,
  output [31:0] out_26,
  output [31:0] out_27,
  output [31:0] out_28,
  output [31:0] out_29,
  output [31:0] out_30,
  output [31:0] out_31,
  output [31:0] out_32,
  output [31:0] out_33,
  output [31:0] out_34,
  output [31:0] out_35,
  output [31:0] out_36
);

  wire Write_check_1, Write_check_2, Write_check_3, Write_check_4, Write_check_5, Write_check_6,
       Write_check_7, Write_check_8, Write_check_9, Write_check_10, Write_check_11, Write_check_12,
       Write_check_13, Write_check_14, Write_check_15, Write_check_16, Write_check_17, Write_check_18,
       Write_check_19, Write_check_20, Write_check_21, Write_check_22, Write_check_23, Write_check_24,
       Write_check_25, Write_check_26, Write_check_27, Write_check_28, Write_check_29, Write_check_30,
       Write_check_31;
  wire [31:0] multiplexer_1_out, multiplexer_2_out, multiplexer_3_out, multiplexer_4_out, multiplexer_5_out,
       multiplexer_6_out, multiplexer_7_out, multiplexer_8_out, multiplexer_9_out, multiplexer_10_out,
       multiplexer_11_out, multiplexer_12_out, multiplexer_13_out, multiplexer_14_out, multiplexer_15_out,
       multiplexer_16_out, multiplexer_17_out, multiplexer_18_out, multiplexer_19_out, multiplexer_20_out,
       multiplexer_21_out, multiplexer_22_out, multiplexer_23_out, multiplexer_24_out, multiplexer_25_out,
       multiplexer_26_out, multiplexer_27_out, multiplexer_28_out, multiplexer_29_out, multiplexer_30_out,
       multiplexer_31_out;

  Write_Chooser write_chooser_1 (
    .Write_Enable(Write_Enable), .Selector(Write_Register), .out_3(Write_check_1), .out_4(Write_check_2),
    .out_5(Write_check_3), .out_6(Write_check_4), .out_7(Write_check_5), .out_8(Write_check_6),
    .out_9(Write_check_7), .out_10(Write_check_8), .out_11(Write_check_9), .out_12(Write_check_10),
    .out_13(Write_check_11), .out_14(Write_check_12), .out_15(Write_check_13), .out_16(Write_check_14),
    .out_17(Write_check_15), .out_18(Write_check_16), .out_19(Write_check_17), .out_20(Write_check_18),
    .out_21(Write_check_19), .out_22(Write_check_20), .out_23(Write_check_21), .out_24(Write_check_22),
    .out_25(Write_check_23), .out_26(Write_check_24), .out_27(Write_check_25), .out_28(Write_check_26),
    .out_29(Write_check_27), .out_30(Write_check_28), .out_31(Write_check_29), .out_32(Write_check_30),
    .out_33(Write_check_31));
  Multiplexer #(.width(32)) multiplexer_1 (
    .in0(out_6), .in1(Write_Data), .out(multiplexer_1_out), .sel(Write_check_1));  // open: en
  Multiplexer #(.width(32)) multiplexer_2 (
    .in0(out_7), .in1(Write_Data), .out(multiplexer_2_out), .sel(Write_check_2));  // open: en
  Multiplexer #(.width(32)) multiplexer_3 (
    .in0(out_8), .in1(Write_Data), .out(multiplexer_3_out), .sel(Write_check_3));  // open: en
  Multiplexer #(.width(32)) multiplexer_4 (
    .in0(out_9), .in1(Write_Data), .out(multiplexer_4_out), .sel(Write_check_4));  // open: en
  Multiplexer #(.width(32)) multiplexer_5 (
    .in0(out_10), .in1(Write_Data), .out(multiplexer_5_out), .sel(Write_check_5));  // open: en
  Multiplexer #(.width(32)) multiplexer_6 (
    .in0(out_11), .in1(Write_Data), .out(multiplexer_6_out), .sel(Write_check_6));  // open: en
  Multiplexer #(.width(32)) multiplexer_7 (
    .in0(out_12), .in1(Write_Data), .out(multiplexer_7_out), .sel(Write_check_7));  // open: en
  Multiplexer #(.width(32)) multiplexer_8 (
    .in0(out_13), .in1(Write_Data), .out(multiplexer_8_out), .sel(Write_check_8));  // open: en
  Register #(.width(32)) _8 (.D(multiplexer_8_out), .Q(out_13), .clk(Clk));  // open: en, clr
  Multiplexer #(.width(32)) multiplexer_9 (
    .in0(out_14), .in1(Write_Data), .out(multiplexer_9_out), .sel(Write_check_9));  // open: en
  Register #(.width(32)) _9 (.D(multiplexer_9_out), .Q(out_14), .clk(Clk));  // open: en, clr
  Register #(.width(32)) _10 (.D(multiplexer_10_out), .Q(out_15), .clk(Clk));  // open: en, clr
  Multiplexer #(.width(32)) multiplexer_10 (
    .in0(out_15), .in1(Write_Data), .out(multiplexer_10_out), .sel(Write_check_10));  // open: en
  Register #(.width(32)) _11 (.D(multiplexer_11_out), .Q(out_16), .clk(Clk));  // open: en, clr
  Multiplexer #(.width(32)) multiplexer_11 (
    .in0(out_16), .in1(Write_Data), .out(multiplexer_11_out), .sel(Write_check_11));  // open: en
  Register #(.width(32)) _12 (.D(multiplexer_12_out), .Q(out_17), .clk(Clk));  // open: en, clr
  Multiplexer #(.width(32)) multiplexer_12 (
    .in0(out_17), .in1(Write_Data), .out(multiplexer_12_out), .sel(Write_check_12));  // open: en
  Register #(.width(32)) _13 (.D(multiplexer_13_out), .Q(out_18), .clk(Clk));  // open: en, clr
  Multiplexer #(.width(32)) multiplexer_13 (
    .in0(out_18), .in1(Write_Data), .out(multiplexer_13_out), .sel(Write_check_13));  // open: en
  Multiplexer #(.width(32)) multiplexer_14 (
    .in0(out_19), .in1(Write_Data), .out(multiplexer_14_out), .sel(Write_check_14));  // open: en
  Register #(.width(32)) _14 (.D(multiplexer_14_out), .Q(out_19), .clk(Clk));  // open: en, clr
  Register #(.width(32)) _15 (.D(multiplexer_15_out), .Q(out_20), .clk(Clk));  // open: en, clr
  Multiplexer #(.width(32)) multiplexer_15 (
    .in0(out_20), .in1(Write_Data), .out(multiplexer_15_out), .sel(Write_check_15));  // open: en
  Multiplexer #(.width(32)) multiplexer_16 (
    .in0(out_21), .in1(Write_Data), .out(multiplexer_16_out), .sel(Write_check_16));  // open: en
  Register #(.width(32)) _16 (.D(multiplexer_16_out), .Q(out_21), .clk(Clk));  // open: en, clr
  Multiplexer #(.width(32)) multiplexer_17 (
    .in0(out_22), .in1(Write_Data), .out(multiplexer_17_out), .sel(Write_check_17));  // open: en
  Register #(.width(32)) _17 (.D(multiplexer_17_out), .Q(out_22), .clk(Clk));  // open: en, clr
  Register #(.width(32)) _18 (.D(multiplexer_18_out), .Q(out_23), .clk(Clk));  // open: en, clr
  Multiplexer #(.width(32)) multiplexer_18 (
    .in0(out_23), .in1(Write_Data), .out(multiplexer_18_out), .sel(Write_check_18));  // open: en
  Multiplexer #(.width(32)) multiplexer_19 (
    .in0(out_24), .in1(Write_Data), .out(multiplexer_19_out), .sel(Write_check_19));  // open: en
  Register #(.width(32)) _19 (.D(multiplexer_19_out), .Q(out_24), .clk(Clk));  // open: en, clr
  Register #(.width(32)) _20 (.D(multiplexer_20_out), .Q(out_25), .clk(Clk));  // open: en, clr
  Multiplexer #(.width(32)) multiplexer_20 (
    .in0(out_25), .in1(Write_Data), .out(multiplexer_20_out), .sel(Write_check_20));  // open: en
  Multiplexer #(.width(32)) multiplexer_21 (
    .in0(out_26), .in1(Write_Data), .out(multiplexer_21_out), .sel(Write_check_21));  // open: en
  Register #(.width(32)) _21 (.D(multiplexer_21_out), .Q(out_26), .clk(Clk));  // open: en, clr
  Register #(.width(32)) _22 (.D(multiplexer_22_out), .Q(out_27), .clk(Clk));  // open: en, clr
  Multiplexer #(.width(32)) multiplexer_22 (
    .in0(out_27), .in1(Write_Data), .out(multiplexer_22_out), .sel(Write_check_22));  // open: en
  Register #(.width(32)) _23 (.D(multiplexer_23_out), .Q(out_28), .clk(Clk));  // open: en, clr
  Multiplexer #(.width(32)) multiplexer_23 (
    .in0(out_28), .in1(Write_Data), .out(multiplexer_23_out), .sel(Write_check_23));  // open: en
  Register #(.width(32)) _24 (.D(multiplexer_24_out), .Q(out_29), .clk(Clk));  // open: en, clr
  Multiplexer #(.width(32)) multiplexer_24 (
    .in0(out_29), .in1(Write_Data), .out(multiplexer_24_out), .sel(Write_check_24));  // open: en
  Multiplexer #(.width(32)) multiplexer_25 (
    .in0(out_30), .in1(Write_Data), .out(multiplexer_25_out), .sel(Write_check_25));  // open: en
  Register #(.width(32)) _25 (.D(multiplexer_25_out), .Q(out_30), .clk(Clk));  // open: en, clr
  Register #(.width(32)) _26 (.D(multiplexer_26_out), .Q(out_31), .clk(Clk));  // open: en, clr
  Multiplexer #(.width(32)) multiplexer_26 (
    .in0(out_31), .in1(Write_Data), .out(multiplexer_26_out), .sel(Write_check_26));  // open: en
  Register #(.width(32)) _27 (.D(multiplexer_27_out), .Q(out_32), .clk(Clk));  // open: en, clr
  Multiplexer #(.width(32)) multiplexer_27 (
    .in0(out_32), .in1(Write_Data), .out(multiplexer_27_out), .sel(Write_check_27));  // open: en
  Register #(.width(32)) _28 (.D(multiplexer_28_out), .Q(out_33), .clk(Clk));  // open: en, clr
  Multiplexer #(.width(32)) multiplexer_28 (
    .in0(out_33), .in1(Write_Data), .out(multiplexer_28_out), .sel(Write_check_28));  // open: en
  Multiplexer #(.width(32)) multiplexer_29 (
    .in0(out_34), .in1(Write_Data), .out(multiplexer_29_out), .sel(Write_check_29));  // open: en
  Register #(.width(32)) _29 (.D(multiplexer_29_out), .Q(out_34), .clk(Clk));  // open: en, clr
  Register #(.width(32)) _30 (.D(multiplexer_30_out), .Q(out_35), .clk(Clk));  // open: en, clr
  Multiplexer #(.width(32)) multiplexer_30 (
    .in0(out_35), .in1(Write_Data), .out(multiplexer_30_out), .sel(Write_check_30));  // open: en
  Register #(.width(32)) _31 (.D(multiplexer_31_out), .Q(out_36), .clk(Clk));  // open: en, clr
  Multiplexer #(.width(32)) multiplexer_31 (
    .in0(out_36), .in1(Write_Data), .out(multiplexer_31_out), .sel(Write_check_31));  // open: en
  Register #(.width(32)) _1 (.D(multiplexer_1_out), .Q(out_6), .clk(Clk));  // open: en, clr
  Register #(.width(32)) _2 (.D(multiplexer_2_out), .Q(out_7), .clk(Clk));  // open: en, clr
  Register #(.width(32)) _3 (.D(multiplexer_3_out), .Q(out_8), .clk(Clk));  // open: en, clr
  Register #(.width(32)) _4 (.D(multiplexer_4_out), .Q(out_9), .clk(Clk));  // open: en, clr
  Register #(.width(32)) _5 (.D(multiplexer_5_out), .Q(out_10), .clk(Clk));  // open: en, clr
  Register #(.width(32)) _6 (.D(multiplexer_6_out), .Q(out_11), .clk(Clk));  // open: en, clr
  Register #(.width(32)) _7 (.D(multiplexer_7_out), .Q(out_12), .clk(Clk));  // open: en, clr

  assign out_5 = {32{1'b0}};

  // Other names for the same wires on the sheet: Clk_tunnel = Clk
endmodule

module Write_Chooser (
  input  Write_Enable,
  input  [4:0] Selector,
  output out_3,
  output out_4,
  output out_5,
  output out_6,
  output out_7,
  output out_8,
  output out_9,
  output out_10,
  output out_11,
  output out_12,
  output out_13,
  output out_14,
  output out_15,
  output out_16,
  output out_17,
  output out_18,
  output out_19,
  output out_20,
  output out_21,
  output out_22,
  output out_23,
  output out_24,
  output out_25,
  output out_26,
  output out_27,
  output out_28,
  output out_29,
  output out_30,
  output out_31,
  output out_32,
  output out_33
);

  Demultiplexer #(.select(5)) demultiplexer_1 (
    .out1(out_3), .out2(out_4), .out3(out_5), .out4(out_6), .out5(out_7), .out6(out_8), .out7(out_9),
    .out8(out_10), .out9(out_11), .out10(out_12), .out11(out_13), .out12(out_14), .out13(out_15),
    .out14(out_16), .out15(out_17), .out16(out_18), .out17(out_19), .out18(out_20), .out19(out_21),
    .out20(out_22), .out21(out_23), .out22(out_24), .out23(out_25), .out24(out_26), .out25(out_27),
    .out26(out_28), .out27(out_29), .out28(out_30), .out29(out_31), .out30(out_32), .out31(out_33),
    .in(Write_Enable), .sel(Selector));  // open: out0, en
endmodule
