// Logisim project cpu.circ as structural Verilog: 3 circuits, main circuit main
module main (
  input  [31:0] INSTRUCTION,
  input  CLOCK,
  output [31:0] FETCH_ADDRESS,
  output [31:0] s0_Value,
  output [31:0] s1_Value,
  output [31:0] s2_Value,
  output [31:0] ra_Value,
  output [31:0] HI_Value,
  output [31:0] LO_Value
);

  wire ALU_Src, and_1_out, and_3_out, and_4_out, beqal, bne, br_exes, branch, flip, is_branch, jal,
       jr_command, jump, lui, main_2_equal, main_2_signed_overflow, md, mem_to_reg, mem_write, nop,
       not_1_out, or_3_out, sign_ext, swinc, w_en;
  wire [1:0] mf_commands, regDest;
  wire [2:0] ALU_OP, op_unit;
  wire [3:0] S;
  wire [4:0] multiplexer_3_out, rd, rs, rt;
  wire [5:0] control, instruction_t;
  wire [10:0] pipelline_q;
  wire [15:0] imm16;
  wire [25:0] j26;
  wire [27:0] shifter_2_out;
  wire [31:0] adder_3_out, adder_4_out, bit_extender_4_out, bit_extender_5_out, busW, jr, main_1_read_data_2,
       main_2_result, main_2_result_2, MEM_p6, multiplexer_1_out, multiplexer_2_out, multiplexer_5_out,
       multiplexer_6_out, multiplexer_7_out, multiplexer_8_out, multiplexer_9_out, multiplexer_10_out,
       multiplexer_11_out, multiplexer_12_out, multiplexer_13_out, multiplexer_14_out, multiplexer_15_out,
       nop_addr, PC_2_q, ra_t, shamt, shifter_1_out, swinc_ink;

  or or_1 (nop, br_exes, jr_command, jump);
  Multiplexer #(.width(32)) multiplexer_1 (
    .in0(INSTRUCTION), .in1({32{1'b0}}), .out(multiplexer_1_out), .sel(nop));  // open: en
  Control control_1 (
    .Instruction(control), .RegDest(regDest), .Sign_ext(sign_ext), .ALU_Src(ALU_Src), .lui(lui),
    .ALU_Op(ALU_OP), .branch(branch), .bne(bne), .jump(jump), .mem_write(mem_write), .mem_to_reg(mem_to_reg),
    .swinc(swinc), .jal(jal), .w_en(w_en), .op_unit(op_unit), .beqal(beqal));
  Register #(.width(32)) pipelline (
    .D(multiplexer_1_out), .Q({control, rs, rt, rd, pipelline_q}), .clk(CLOCK));  // open: en, clr
  Bit_Extender #(.in_width(32)) bit_extender_1 (.in({control, rs, rt, rd, pipelline_q}), .out(imm16));
  Bit_Extender #(.in_width(32), .out_width(26)) bit_extender_2 (.in({control, rs, rt, rd, pipelline_q}), .out(j26));
  assign shamt = {{27{1'b0}}, pipelline_q[10:6]};  // Bit_Extender bit_extender_3
  Multiplexer #(.width(32)) multiplexer_2 (
    .in0(nop_addr), .in1(multiplexer_11_out), .out(multiplexer_2_out), .sel(nop));  // open: en
  Register #(.width(32)) PC (.D(multiplexer_2_out), .Q(FETCH_ADDRESS), .clk(CLOCK));  // open: en, clr
  Adder #(.width(32)) adder_1 (.a(FETCH_ADDRESS), .b(32'h4), .out(nop_addr));  // open: cin, cout
  Register #(.width(32)) PC_2 (.D(FETCH_ADDRESS), .Q(PC_2_q), .clk(CLOCK));  // open: en, clr
  Multiplexer #(.select(2), .width(5)) multiplexer_3 (
    .in0(rt), .in1(rd), .in2({5{1'b1}}), .in3(rs), .out(multiplexer_3_out), .sel(regDest));  // open: en
  assign bit_extender_4_out = {{16{1'b0}}, imm16};  // Bit_Extender bit_extender_4
  assign bit_extender_5_out = {{16{imm16[15]}}, imm16};  // Bit_Extender bit_extender_5
  Bit_Extender #(.in_width(16), .out_width(6)) bit_extender_6 (.in(imm16), .out(instruction_t));
  Adder #(.width(32)) adder_2 (.a(PC_2_q), .b(32'h4), .out(ra_t));  // open: cin, cout
  regfile_main main_1 (
    .Read_Register_1(rs), .Read_Register_2(rt), .Write_Register(multiplexer_3_out), .Write_Data(busW),
    .Write_Enable(and_1_out), .Clock(CLOCK), .Read_Data_1(jr), .Read_Data_2(main_1_read_data_2),
    .s0_Value(s0_Value), .s1_Value(s1_Value), .s2_Value(s2_Value), .ra_Value(ra_Value));
  and and_1 (and_1_out, w_en, ~md);  // AND_Gate
  Multiplexer #(.width(32)) multiplexer_4 (
    .in0(bit_extender_4_out), .in1(bit_extender_5_out), .out(swinc_ink), .sel(sign_ext));  // open: en
  Adder #(.width(32)) adder_3 (.a(ra_t), .b(shifter_1_out), .out(adder_3_out));  // open: cin, cout
  Shifter #(.width(32)) shifter_1 (.in(swinc_ink), .\dist (5'b00010), .out(shifter_1_out));
  Multiplexer #(.width(32), .enable("false")) multiplexer_5 (
    .in0(jr), .in1(multiplexer_6_out), .out(multiplexer_5_out), .sel(flip));
  Multiplexer #(.width(32)) multiplexer_6 (
    .in0(main_1_read_data_2), .in1(swinc_ink), .out(multiplexer_6_out), .sel(ALU_Src));  // open: en
  Multiplexer #(.width(32), .enable("false")) multiplexer_7 (
    .in0(multiplexer_6_out), .in1(shamt), .out(multiplexer_7_out), .sel(flip));
  Shifter #(.width(28)) shifter_2 (.in({2'b00, j26}), .\dist (5'b00010), .out(shifter_2_out));
  or or_2 (br_exes, is_branch, and_3_out);
  and and_2 (is_branch, branch, main_2_equal);
  Multiplexer #(.width(32), .enable("false")) multiplexer_8 (
    .in0(multiplexer_7_out), .in1(32'h10), .out(multiplexer_8_out), .sel(lui));
  ALU_Control ALU_R_CTRL (
    .ALU_OP(ALU_OP), .OP(instruction_t), .To_ALU(S), .md(md), .jr(jr_command), .mf__commands(mf_commands),
    .flip(flip));
  Multiplexer #(.width(32)) multiplexer_9 (
    .in0(ra_t), .in1(adder_3_out), .out(multiplexer_9_out), .sel(br_exes));  // open: en
  and and_3 (and_3_out, not_1_out, bne);
  not not_1 (not_1_out, main_2_equal);
  LED led_1 (.in(main_2_signed_overflow));
  alu_main main_2 (
    .Switch(S), .X(multiplexer_5_out), .Equal(main_2_equal), .Result(main_2_result),
    .Signed_Overflow(main_2_signed_overflow), .Y(multiplexer_8_out), .Result_2(main_2_result_2));
  Multiplexer #(.width(32)) multiplexer_10 (
    .in0(multiplexer_9_out), .in1({ra_t[31:28], shifter_2_out}), .out(multiplexer_10_out), .sel(jump));  // open: en
  Register #(.width(32)) LO (.D(main_2_result), .en(md), .Q(LO_Value), .clk(CLOCK));  // open: clr
  Register #(.width(32)) HI (.D(main_2_result_2), .en(md), .Q(HI_Value), .clk(CLOCK));  // open: clr
  Multiplexer #(.width(32)) multiplexer_11 (
    .in0(multiplexer_10_out), .in1(jr), .out(multiplexer_11_out), .sel(jr_command));  // open: en
  Multiplexer #(.select(2), .width(32)) multiplexer_12 (
    .in0(main_2_result), .in1(LO_Value), .in2(HI_Value), .in3(HI_Value), .out(multiplexer_12_out),
    .sel(mf_commands));  // open: en
  Adder #(.width(32)) adder_4 (.a(swinc_ink), .b(jr), .out(adder_4_out));  // open: cin, cout
  // mem_main MEM: pin names not known; wires that end beside it: multiplexer_12_out, main_1_read_data_2, mem_write, CLOCK, op_unit, MEM_p6
  Multiplexer #(.width(32)) multiplexer_13 (
    .in0(multiplexer_12_out), .in1(MEM_p6), .out(multiplexer_13_out), .sel(mem_to_reg));  // open: en
  Multiplexer #(.width(32), .enable("false")) multiplexer_14 (
    .in0(multiplexer_13_out), .in1(adder_4_out), .out(multiplexer_14_out), .sel(swinc));
  Multiplexer #(.width(32)) multiplexer_15 (
    .in0(multiplexer_14_out), .in1(ra_t), .out(multiplexer_15_out), .sel(or_3_out));  // open: en
  or or_3 (or_3_out, jal, beqal);
  Multiplexer #(.width(32), .enable("false")) multiplexer_16 (
    .in0(multiplexer_15_out), .in1(ra_Value), .out(busW), .sel(and_4_out));
  and and_4 (and_4_out, ~is_branch, beqal);  // AND_Gate

  // Other names for the same wires on the sheet: clk = CLOCK; fetch_addr[31:0] = FETCH_ADDRESS; HI[31:0] = HI_Value;
  //   LO[31:0] = LO_Value; ra[31:0] = ra_Value; s0[31:0] = s0_Value; s1[31:0] = s1_Value; s2[31:0] = s2_Value

  // Notes on the sheet:
  //   Output
  //   These are outputs/inputs from run.circ
  //   Inputs
  //   These are DEBUG/TEST outputs from your circuit.
endmodule

module ALU_Control (
  input  [2:0] ALU_OP,
  input  [5:0] OP,
  output [3:0] To_ALU,
  output md,
  output jr,
  output [1:0] mf__commands,
  output flip
);

  wire add_A_out, add_R_out, addu_A_out, addu_R_out, and_A_out, and_R_out, divu_R_out, multu_R_out, or_1_out,
       or_2_out, or_3_out, or_4_out, or_5_out, or_6_out, or_A_out, or_R_out, sll_A_out, sll_R_out, slt_A_out,
       slt_R_out, sltu_R_out, sra_R_out, srl_R_out, sub_R_out, subu_R_out;

  and sll_R (sll_R_out, ALU_OP[2], ~ALU_OP[1], ~ALU_OP[0], ~OP[5], ~OP[4], ~OP[3], ~OP[2], ~OP[1], ~OP[0]);  // AND_Gate
  or or_1 (or_1_out, sll_R_out, sll_A_out);
  and sll_A (sll_A_out, ALU_OP[2], ~ALU_OP[1], ALU_OP[0]);  // AND_Gate
  and srl_R (srl_R_out, ALU_OP[2], ~ALU_OP[1], ~ALU_OP[0], ~OP[5], ~OP[4], ~OP[3], ~OP[2], OP[1], ~OP[0]);  // AND_Gate
  and sra_R (sra_R_out, ALU_OP[2], ~ALU_OP[1], ~ALU_OP[0], ~OP[5], ~OP[4], ~OP[3], ~OP[2], OP[1], OP[0]);  // AND_Gate
  and multu_R (multu_R_out, ALU_OP[2], ~ALU_OP[1], ~ALU_OP[0], ~OP[5], OP[4], OP[3], ~OP[2], ~OP[1], OP[0]);  // AND_Gate
  and divu_R (divu_R_out, ALU_OP[2], ~ALU_OP[1], ~ALU_OP[0], ~OP[5], OP[4], OP[3], ~OP[2], OP[1], OP[0]);  // AND_Gate
  and add_R (add_R_out, ALU_OP[2], ~ALU_OP[1], ~ALU_OP[0], OP[5], ~OP[4], ~OP[3], ~OP[2], ~OP[1], ~OP[0]);  // AND_Gate
  or or_2 (or_2_out, add_R_out, add_A_out);
  and add_A (add_A_out, ~ALU_OP[2], ~ALU_OP[1], ALU_OP[0]);  // AND_Gate
  and addu_R (addu_R_out, ALU_OP[2], ~ALU_OP[1], ~ALU_OP[0], OP[5], ~OP[4], ~OP[3], ~OP[2], ~OP[1], OP[0]);  // AND_Gate
  or or_3 (or_3_out, addu_R_out, addu_A_out);
  and addu_A (addu_A_out, ~ALU_OP[2], ALU_OP[1], ~ALU_OP[0]);  // AND_Gate
  and sub_R (sub_R_out, ALU_OP[2], ~ALU_OP[1], ~ALU_OP[0], OP[5], ~OP[4], ~OP[3], ~OP[2], OP[1], ~OP[0]);  // AND_Gate
  and subu_R (subu_R_out, ALU_OP[2], ~ALU_OP[1], ~ALU_OP[0], OP[5], ~OP[4], ~OP[3], ~OP[2], OP[1], OP[0]);  // AND_Gate
  and and_R (and_R_out, ALU_OP[2], ~ALU_OP[1], ~ALU_OP[0], OP[5], ~OP[4], ~OP[3], OP[2], ~OP[1], ~OP[0]);  // AND_Gate
  or or_4 (or_4_out, and_R_out, and_A_out);
  and and_A (and_A_out, ~ALU_OP[2], ALU_OP[1], ALU_OP[0]);  // AND_Gate
  and or_R (or_R_out, ALU_OP[2], ~ALU_OP[1], ~ALU_OP[0], OP[5], ~OP[4], ~OP[3], OP[2], ~OP[1], OP[0]);  // AND_Gate
  and or_A (or_A_out, ALU_OP[2], ALU_OP[1], ~ALU_OP[0]);  // AND_Gate
  or or_5 (or_5_out, or_R_out, or_A_out);
  and slt_R (slt_R_out, ALU_OP[2], ~ALU_OP[1], ~ALU_OP[0], OP[5], ~OP[4], OP[3], ~OP[2], OP[1], ~OP[0]);  // AND_Gate
  and slt_A (slt_A_out, ALU_OP[2], ALU_OP[1], ALU_OP[0]);
  or or_6 (or_6_out, slt_R_out, slt_A_out);
  and sltu_R (sltu_R_out, ALU_OP[2], ~ALU_OP[1], ~ALU_OP[0], OP[5], ~OP[4], OP[3], ~OP[2], OP[1], OP[0]);  // AND_Gate
  and u_jr (jr, ALU_OP[2], ~ALU_OP[1], ~ALU_OP[0], ~OP[5], ~OP[4], OP[3], ~OP[2], ~OP[1], ~OP[0]);  // AND_Gate
  and mfhi (mf__commands[1], ALU_OP[2], ~ALU_OP[1], ~ALU_OP[0], ~OP[5], OP[4], ~OP[3], ~OP[2], ~OP[1], ~OP[0]);  // AND_Gate
  and mflo (mf__commands[0], ALU_OP[2], ~ALU_OP[1], ~ALU_OP[0], ~OP[5], OP[4], ~OP[3], ~OP[2], OP[1], ~OP[0]);  // AND_Gate
  or or_7 (To_ALU[0], srl_R_out, multu_R_out, or_2_out, sub_R_out, or_4_out, or_6_out);
  or or_8 (To_ALU[1], sra_R_out, multu_R_out, or_3_out, sub_R_out, or_5_out, or_6_out);
  or or_9 (To_ALU[2], divu_R_out, or_2_out, or_3_out, sub_R_out, sltu_R_out);
  or or_10 (To_ALU[3], subu_R_out, or_4_out, or_5_out, or_6_out, sltu_R_out);
  or or_11 (md, multu_R_out, divu_R_out);
  or or_12 (flip, or_1_out, srl_R_out, sra_R_out);
endmodule

module Control (
  input  [5:0] Instruction,
  output [1:0] RegDest,
  output Sign_ext,
  output ALU_Src,
  output lui,
  output [2:0] ALU_Op,
  output branch,
  output bne,
  output jump,
  output mem_write,
  output mem_to_reg,
  output swinc,
  output jal,
  output w_en,
  output [2:0] op_unit,
  output beqal
);

  wire addi_out, addiu_out, andi_out, beq_out, j_out, lb_out, lbu_out, lhu_out, lw_out, ori_out, R_Type_out,
       sb_out, sh_out, slti_out, sw_out;

  and R_Type (R_Type_out, ~Instruction[5], ~Instruction[4], ~Instruction[3], ~Instruction[2], ~Instruction[1], ~Instruction[0]);  // AND_Gate
  and addi (addi_out, ~Instruction[5], ~Instruction[4], Instruction[3], ~Instruction[2], ~Instruction[1], ~Instruction[0]);  // AND_Gate
  and addiu (addiu_out, ~Instruction[5], ~Instruction[4], Instruction[3], ~Instruction[2], ~Instruction[1], Instruction[0]);  // AND_Gate
  and andi (andi_out, ~Instruction[5], ~Instruction[4], Instruction[3], Instruction[2], ~Instruction[1], ~Instruction[0]);  // AND_Gate
  and beq (beq_out, ~Instruction[5], ~Instruction[4], ~Instruction[3], Instruction[2], ~Instruction[1], ~Instruction[0]);  // AND_Gate
  and u_beqal (beqal, ~Instruction[5], Instruction[4], ~Instruction[3], Instruction[2], ~Instruction[1], ~Instruction[0]);  // AND_Gate
  and u_bne (bne, ~Instruction[5], ~Instruction[4], ~Instruction[3], Instruction[2], ~Instruction[1], Instruction[0]);  // AND_Gate
  and j (j_out, ~Instruction[5], ~Instruction[4], ~Instruction[3], ~Instruction[2], Instruction[1], ~Instruction[0]);  // AND_Gate
  and u_jal (jal, ~Instruction[5], ~Instruction[4], ~Instruction[3], ~Instruction[2], Instruction[1], Instruction[0]);  // AND_Gate
  and lb (lb_out, Instruction[5], ~Instruction[4], ~Instruction[3], ~Instruction[2], ~Instruction[1], ~Instruction[0]);  // AND_Gate
  and lbu (lbu_out, Instruction[5], ~Instruction[4], ~Instruction[3], Instruction[2], ~Instruction[1], ~Instruction[0]);  // AND_Gate
  and lhu (lhu_out, Instruction[5], ~Instruction[4], ~Instruction[3], Instruction[2], ~Instruction[1], Instruction[0]);  // AND_Gate
  and u_lui (lui, ~Instruction[5], ~Instruction[4], Instruction[3], Instruction[2], Instruction[1], Instruction[0]);  // AND_Gate
  and lw (lw_out, Instruction[5], ~Instruction[4], ~Instruction[3], ~Instruction[2], Instruction[1], Instruction[0]);  // AND_Gate
  and ori (ori_out, ~Instruction[5], ~Instruction[4], Instruction[3], Instruction[2], ~Instruction[1], Instruction[0]);  // AND_Gate
  and slti (slti_out, ~Instruction[5], ~Instruction[4], Instruction[3], ~Instruction[2], Instruction[1], ~Instruction[0]);  // AND_Gate
  and sb (sb_out, Instruction[5], ~Instruction[4], Instruction[3], ~Instruction[2], ~Instruction[1], ~Instruction[0]);  // AND_Gate
  and sh (sh_out, Instruction[5], ~Instruction[4], Instruction[3], ~Instruction[2], ~Instruction[1], Instruction[0]);  // AND_Gate
  and sw (sw_out, Instruction[5], ~Instruction[4], Instruction[3], ~Instruction[2], Instruction[1], Instruction[0]);  // AND_Gate
  and u_swinc (swinc, Instruction[5], ~Instruction[4], Instruction[3], Instruction[2], ~Instruction[1], ~Instruction[0]);  // AND_Gate
  or or_1 (op_unit[0], lb_out, sb_out);
  or or_2 (op_unit[1], lhu_out, sh_out);
  or or_3 (op_unit[2], lw_out, sw_out, swinc);
  or or_4 (RegDest[0], R_Type_out, swinc);
  or or_5 (RegDest[1], swinc, beqal, jal);
  or or_6 (ALU_Op[0], addi_out, andi_out, lb_out, lbu_out, lhu_out, lui, lw_out, slti_out, sb_out, sh_out, sw_out, swinc);
  or or_7 (ALU_Op[1], addiu_out, andi_out, ori_out, slti_out);
  or or_8 (ALU_Op[2], R_Type_out, lui, ori_out, slti_out);
  or or_9 (branch, beq_out, beqal);
  or or_10 (jump, j_out, jal);
  or or_11 (mem_write, sb_out, sh_out, sw_out, swinc);
  or or_12 (mem_to_reg, lb_out, lbu_out, lhu_out, lw_out);
  or or_13 (w_en, R_Type_out, addi_out, addiu_out, andi_out, beqal, jal, lb_out, lbu_out, lhu_out, lui, lw_out, ori_out, slti_out, swinc);
  or or_14 (Sign_ext, addi_out, addiu_out, beq_out, beqal, bne, lb_out, lbu_out, lhu_out, lw_out, slti_out, sb_out, sh_out, sw_out, swinc);
  nor nor_1 (ALU_Src, R_Type_out, beq_out, beqal, bne);
endmodule
