// Logisim project alu.circ as structural Verilog: 1 circuit, main circuit main
module main (
  input  [31:0] X,
  input  [31:0] Y,
  input  [3:0] Switch,
  output Signed_Overflow,
  output Equal,
  output [31:0] Result,
  output [31:0] Result_2
);

  wire adder_1_cout, adder_2_cout, adder_3_cout, adder_4_cout, comparator_1_lt, comparator_2_lt,
       overflow_add, overflow_sub;
  wire [4:0] bit_extender_1_out, bit_extender_2_out, bit_extender_3_out;
  wire [31:0] add, addu, \and , div_hi, div_lo, mul_hi, mul_lo, \or , sll, slt, sltu, sra, srl, sub, subu,
       xor_1_out;

  Comparator #(.width(32)) comparator_1 (.a(X), .b(Y), .eq(Equal), .lt(comparator_1_lt));  // open: gt
  Comparator #(.width(32), .mode("unsigned")) comparator_2 (.a(X), .b(Y), .lt(comparator_2_lt));  // open: gt, eq
  Bit_Extender #(.in_width(32), .out_width(5)) bit_extender_1 (.in(Y), .out(bit_extender_1_out));
  Bit_Extender #(.in_width(32), .out_width(5)) bit_extender_2 (.in(Y), .out(bit_extender_2_out));
  Bit_Extender #(.in_width(32), .out_width(5)) bit_extender_3 (.in(Y), .out(bit_extender_3_out));
  assign slt = {{31{1'b0}}, comparator_1_lt};  // Bit_Extender bit_extender_4
  assign sltu = {{31{1'b0}}, comparator_2_lt};  // Bit_Extender bit_extender_5
  Shifter #(.width(32)) shifter_1 (.in(X), .\dist (bit_extender_1_out), .out(sll));
  Shifter #(.width(32), .shift("lr")) shifter_2 (.in(X), .\dist (bit_extender_2_out), .out(srl));
  Shifter #(.width(32), .shift("ar")) shifter_3 (.in(X), .\dist (bit_extender_3_out), .out(sra));
  Multiplier #(.width(32)) multiplier_1 (.a(X), .b(Y), .out(mul_lo), .cout(mul_hi));  // open: cin
  Divider #(.width(32)) divider_1 (.a(X), .b(Y), .out(div_lo), .rem(div_hi));  // open: upper
  assign xor_1_out = Y ^ {32{1'b1}};  // XOR_Gate xor_1, 32 bits wide
  assign \and  = X & Y;  // AND_Gate and_1, 32 bits wide
  assign \or  = X | Y;  // OR_Gate or_1, 32 bits wide
  Adder #(.width(31)) adder_1 (.a(X[30:0]), .b(Y[30:0]), .out(add[30:0]), .cout(adder_1_cout));  // open: cin
  Adder #(.width(1)) adder_2 (.a(X[31]), .b(Y[31]), .out(add[31]), .cin(adder_1_cout), .cout(adder_2_cout));
  Adder #(.width(31)) adder_3 (.a(X[30:0]), .b(xor_1_out[30:0]), .out(sub[30:0]), .cin(1'b1), .cout(adder_3_cout));
  Adder #(.width(1)) adder_4 (.a(X[31]), .b(xor_1_out[31]), .out(sub[31]), .cin(adder_3_cout), .cout(adder_4_cout));
  xor xor_2 (overflow_add, adder_1_cout, adder_2_cout);
  Multiplexer #(.select(4), .width(32)) multiplexer_1 (
    .in0(sll), .in1(srl), .in2(sra), .in3(mul_lo), .in4(div_lo), .in5(add), .in6(addu), .in7(sub),
    .in8(subu), .in9(\and ), .in10(\or ), .in11(slt), .in12(sltu), .in13({32{1'b0}}), .in14({32{1'b0}}),
    .in15({32{1'b0}}), .out(Result), .sel(Switch));  // open: en
  Multiplexer #(.select(4), .width(32)) multiplexer_2 (
    .in0({32{1'b0}}), .in1({32{1'b0}}), .in2({32{1'b0}}), .in3(mul_hi), .in4(div_hi), .in5({32{1'b0}}),
    .in6({32{1'b0}}), .in7({32{1'b0}}), .in8({32{1'b0}}), .in9({32{1'b0}}), .in10({32{1'b0}}),
    .in11({32{1'b0}}), .in12({32{1'b0}}), .in13({32{1'b0}}), .in14({32{1'b0}}), .in15({32{1'b0}}),
    .out(Result_2), .sel(Switch));  // open: en
  xor xor_3 (overflow_sub, adder_3_cout, adder_4_cout);
  Multiplexer #(.select(4)) multiplexer_3 (
    .in0(1'b0), .in1(1'b0), .in2(1'b0), .in3(1'b0), .in4(1'b0), .in5(overflow_add), .in6(1'b0),
    .in7(overflow_sub), .in8(1'b0), .in9(1'b0), .in10(1'b0), .in11(1'b0), .in12(1'b0), .in13(1'b0),
    .in14(1'b0), .in15(1'b0), .out(Signed_Overflow), .sel(Switch));  // open: en
  Adder #(.width(32)) adder_5 (.a(X), .b(Y), .out(addu));  // open: cin, cout
  Subtractor #(.width(32)) subtractor_1 (.a(X), .b(Y), .out(subu));  // open: bin, bout

  // Other names for the same wires on the sheet: overflow = Signed_Overflow; S[3:0] = Switch

  // Notes on the sheet:
  //   INPUTS to your circuit
  //   DON'T CHANGE THE LOCATIONS OF THE INPUTS AND OUTPUTS!
  //   OUTPUTS from your circuit
endmodule
